// Logisim project CPU (1).circ as structural Verilog: 1 circuit, main circuit main
module main (
);

  wire n7404_1_pin1, n7404_2_pin12, n7404_3_pin2, n7404_3_pin4, n7404_4_pin2, n7404_4_pin4, n7404_4_pin6,
       n7404_4_pin8, n7404_4_pin10, n7404_4_pin12, n7404_5_pin2, n7404_5_pin4, n7404_5_pin6, n7404_5_pin8,
       n7404_5_pin10, n7404_5_pin12, n7404_6_pin12, n7404_7_pin12, n7408_1_pin8, n7408_1_pin9, n7408_1_pin11,
       n7408_1_pin12, n7408_1_pin13, n7408_2_pin12, n7408_3_pin8, n7408_3_pin9, n7408_3_pin11, n7408_4_pin9,
       n7408_5_pin9, n7408_8_pin6, n7408_9_pin3, n7408_9_pin6, n7408_9_pin11, n7408_9_pin12, n7432_1_pin3,
       n7432_1_pin6, n7432_2_pin9, n7432_2_pin10, n7432_3_pin3, n7447_1_pin1, n7447_1_pin2, n7447_1_pin6,
       n7447_1_pin7, n7447_1_pin9, n7447_1_pin10, n7447_1_pin11, n7447_1_pin12, n7447_1_pin13, n7447_1_pin14,
       n7447_1_pin15, n7447_2_pin9, n7447_2_pin10, n7447_2_pin11, n7447_2_pin12, n7447_2_pin13,
       n7447_2_pin14, n7447_2_pin15, n7474_1_pin5, n7474_1_pin9, n7474_2_pin3, n7474_2_pin5, n7474_2_pin9,
       n7474_3_pin3, n7474_3_pin5, n7474_3_pin9, n7474_4_pin3, n7474_4_pin5, n7474_4_pin9, n7474_5_pin5,
       n7474_6_pin5, n7474_7_pin5, n7474_8_pin5, n7485_1_pin1, n7485_2_pin1, n7485_3_pin5, n7485_3_pin7,
       n7485_4_pin5, n7485_4_pin7, n7486_1_pin9, n7486_1_pin10, n7486_2_pin9, n7486_2_pin10, n7486_6_pin6,
       n74138_1_pin4, n74138_1_pin7, n74138_1_pin9, n74138_1_pin10, n74138_1_pin11, n74138_1_pin12,
       n74138_1_pin13, n74138_1_pin14, n74138_1_pin15, n74138_2_pin4, n74138_2_pin7, n74138_2_pin9,
       n74138_2_pin10, n74138_2_pin11, n74138_2_pin12, n74138_2_pin13, n74138_2_pin14, n74138_2_pin15,
       n74157_1_pin1, n74157_1_pin2, n74157_1_pin5, n74157_1_pin11, n74157_1_pin14, n74157_2_pin2,
       n74157_2_pin5, n74157_2_pin11, n74157_2_pin14, n74157_3_pin2, n74157_3_pin3, n74157_3_pin5,
       n74157_3_pin11, n74157_3_pin14, n74157_4_pin2, n74157_4_pin5, n74157_4_pin11, n74157_4_pin14,
       n74157_5_pin3, n74157_5_pin6, n74157_5_pin10, n74157_5_pin13, n74245_1_pin1, n74245_1_pin11,
       n74245_1_pin12, n74245_1_pin13, n74245_1_pin14, n74245_2_pin1, n74283_1_pin9;
  wire [3:0] n74157_1_pin4, n74157_2_pin4, n74157_3_pin4, n74157_4_pin4;
  wire [6:0] n7474_12_pin9;
  wire [7:0] n7408_6_pin3, n7474_12_pin12, n7486_3_pin3, n74157_5_pin4, n74245_1_pin2, n74283_1_pin4;
  wire [7:7] n7474_9_pin5;
  wire [8:8] n74283_2_pin9;
  wire [15:0] Instructions_data;

  _74157 #(.ShowInternalStructure("true")) u_74157_1 (
    .pin1(n74157_1_pin1), .pin2(n74157_1_pin2), .pin3(Instructions_data[0]), .pin4(n74157_1_pin4[0]),
    .pin5(n74157_1_pin5), .pin6(Instructions_data[1]), .pin7(n74157_1_pin4[1]), .pin14(n74157_1_pin14),
    .pin13(Instructions_data[3]), .pin12(n74157_1_pin4[3]), .pin11(n74157_1_pin11),
    .pin10(Instructions_data[2]), .pin9(n74157_1_pin4[2]));  // open: pin15
  _74157 #(.ShowInternalStructure("true")) u_74157_2 (
    .pin1(n74157_1_pin1), .pin2(n74157_2_pin2), .pin3(Instructions_data[4]), .pin4(n74157_2_pin4[0]),
    .pin5(n74157_2_pin5), .pin6(Instructions_data[5]), .pin7(n74157_2_pin4[1]), .pin14(n74157_2_pin14),
    .pin13(Instructions_data[7]), .pin12(n74157_2_pin4[3]), .pin11(n74157_2_pin11),
    .pin10(Instructions_data[6]), .pin9(n74157_2_pin4[2]));  // open: pin15
  _74670 #(.ShowInternalStructure("true")) u_74670_1 ();  // open: pin1, pin2, pin3, pin4, pin5, pin6, pin7, pin15, pin14, pin13, pin12, pin11, pin10, pin9
  _74157 #(.ShowInternalStructure("true")) u_74157_3 (
    .pin1(n74157_1_pin1), .pin2(n74157_3_pin2), .pin3(n74157_3_pin3), .pin4(n74157_3_pin4[0]),
    .pin5(n74157_3_pin5), .pin7(n74157_3_pin4[1]), .pin14(n74157_3_pin14), .pin13(n74157_3_pin3),
    .pin12(n74157_3_pin4[3]), .pin11(n74157_3_pin11), .pin10(n74157_3_pin3), .pin9(n74157_3_pin4[2]));  // open: pin6, pin15
  _7447 #(.ShowInternalStructure("true")) u_7447_1 (
    .pin1(n7447_1_pin1), .pin2(n7447_1_pin2), .pin6(n7447_1_pin6), .pin7(n7447_1_pin7),
    .pin15(n7447_1_pin15), .pin14(n7447_1_pin14), .pin13(n7447_1_pin13), .pin12(n7447_1_pin12),
    .pin11(n7447_1_pin11), .pin10(n7447_1_pin10), .pin9(n7447_1_pin9));  // open: pin3, pin4, pin5
  _7_Segment_Display #(.active("false"), .decimalPoint("false")) u_7_segment_display_1 (
    .g(n7447_1_pin14), .f(n7447_1_pin15), .a(n7447_1_pin13), .b(n7447_1_pin12), .e(n7447_1_pin9),
    .d(n7447_1_pin10), .c(n7447_1_pin11));
  _74157 #(.ShowInternalStructure("true")) u_74157_4 (
    .pin1(n74157_1_pin1), .pin2(n74157_4_pin2), .pin3(n74157_3_pin3), .pin4(n74157_4_pin4[0]),
    .pin5(n74157_4_pin5), .pin6(n74157_3_pin3), .pin7(n74157_4_pin4[1]), .pin14(n74157_4_pin14),
    .pin13(n74157_3_pin3), .pin12(n74157_4_pin4[3]), .pin11(n74157_4_pin11), .pin10(n74157_3_pin3),
    .pin9(n74157_4_pin4[2]));  // open: pin15
  _7447 #(.ShowInternalStructure("true")) u_7447_2 (
    .pin1(n74157_1_pin4[1]), .pin2(n74157_1_pin4[2]), .pin6(n74157_1_pin4[3]), .pin7(n74157_1_pin4[0]),
    .pin15(n7447_2_pin15), .pin14(n7447_2_pin14), .pin13(n7447_2_pin13), .pin12(n7447_2_pin12),
    .pin11(n7447_2_pin11), .pin10(n7447_2_pin10), .pin9(n7447_2_pin9));  // open: pin3, pin4, pin5
  Hex_Digit_Display #(.decimalPoint("false")) hex_digit_display_1 (.value(n74157_4_pin4));
  _7408 #(.ShowInternalStructure("true")) u_7408_1 (
    .pin13(n7408_1_pin13), .pin12(n7408_1_pin12), .pin11(n7408_1_pin11), .pin10(n7408_1_pin11),
    .pin9(n7408_1_pin9), .pin8(n7408_1_pin8));  // open: pin1, pin2, pin3, pin4, pin5, pin6
  // Digital_Oscilloscope digital_oscilloscope_1: pin names not known; wires that end beside it: n7408_1_pin8
  _7_Segment_Display #(.active("false"), .decimalPoint("false")) u_7_segment_display_2 (
    .g(n7447_2_pin14), .f(n7447_2_pin15), .a(n7447_2_pin13), .b(n7447_2_pin12), .e(n7447_2_pin9),
    .d(n7447_2_pin10), .c(n7447_2_pin11));
  Hex_Digit_Display #(.decimalPoint("false")) hex_digit_display_2 (.value(n74157_3_pin4));
  Hex_Digit_Display #(.decimalPoint("false")) hex_digit_display_3 (.value(n74157_2_pin4));
  _7404 #(.ShowInternalStructure("true")) u_7404_1 (
    .pin1(n7404_1_pin1), .pin2(n7408_1_pin12), .pin3(n74157_1_pin1), .pin4(n7408_1_pin9));  // open: pin5, pin6, pin13, pin12, pin11, pin10, pin9, pin8
  Clock clock_1 (.out(n7408_1_pin13));
  Hex_Digit_Display #(.decimalPoint("false")) hex_digit_display_4 (.value(n74157_1_pin4));
  _7474 #(.ShowInternalStructure("true")) u_7474_1 (
    .pin2(n74157_1_pin2), .pin3(n7408_1_pin8), .pin5(n7474_1_pin5), .pin6(n74157_1_pin2),
    .pin12(n74157_1_pin5), .pin11(n7474_1_pin5), .pin9(n7474_1_pin9), .pin8(n74157_1_pin5));  // open: pin1, pin4, pin13, pin10
  _7474 u_7474_2 (
    .pin2(n74157_2_pin2), .pin3(n7474_2_pin3), .pin5(n7474_2_pin5), .pin6(n74157_2_pin2),
    .pin12(n74157_2_pin5), .pin11(n7474_2_pin5), .pin9(n7474_2_pin9), .pin8(n74157_2_pin5));  // open: pin1, pin4, pin13, pin10
  _7474 u_7474_3 (
    .pin2(n74157_3_pin2), .pin3(n7474_3_pin3), .pin5(n7474_3_pin5), .pin6(n74157_3_pin2),
    .pin12(n74157_3_pin5), .pin11(n7474_3_pin5), .pin9(n7474_3_pin9), .pin8(n74157_3_pin5));  // open: pin1, pin4, pin13, pin10
  _7474 u_7474_4 (
    .pin2(n74157_4_pin2), .pin3(n7474_4_pin3), .pin5(n7474_4_pin5), .pin6(n74157_4_pin2),
    .pin12(n74157_4_pin5), .pin11(n7474_4_pin5), .pin9(n7474_4_pin9), .pin8(n74157_4_pin5));  // open: pin1, pin4, pin13, pin10
  _7474 #(.ShowInternalStructure("true")) u_7474_5 (
    .pin2(n74157_1_pin11), .pin3(n7474_1_pin9), .pin5(n7474_5_pin5), .pin6(n74157_1_pin11),
    .pin12(n74157_1_pin14), .pin11(n7474_5_pin5), .pin9(n7474_2_pin3), .pin8(n74157_1_pin14));  // open: pin1, pin4, pin13, pin10
  _7474 u_7474_6 (
    .pin2(n74157_2_pin11), .pin3(n7474_2_pin9), .pin5(n7474_6_pin5), .pin6(n74157_2_pin11),
    .pin12(n74157_2_pin14), .pin11(n7474_6_pin5), .pin9(n7474_3_pin3), .pin8(n74157_2_pin14));  // open: pin1, pin4, pin13, pin10
  _7474 u_7474_7 (
    .pin2(n74157_3_pin11), .pin3(n7474_3_pin9), .pin5(n7474_7_pin5), .pin6(n74157_3_pin11),
    .pin12(n74157_3_pin14), .pin11(n7474_7_pin5), .pin9(n7474_4_pin3), .pin8(n74157_3_pin14));  // open: pin1, pin4, pin13, pin10
  _7474 #(.ShowInternalStructure("true")) u_7474_8 (
    .pin2(n74157_4_pin11), .pin3(n7474_4_pin9), .pin5(n7474_8_pin5), .pin6(n74157_4_pin11),
    .pin12(n74157_4_pin14), .pin11(n7474_8_pin5), .pin8(n74157_4_pin14));  // open: pin1, pin4, pin13, pin10, pin9
  ROM #(.addrWidth(16), .dataWidth(16)) Instructions (
    .addr({n74157_4_pin4, n74157_3_pin4, n74157_2_pin4, n74157_1_pin4}), .data(Instructions_data));
  _7404 #(.ShowInternalStructure("true")) u_7404_2 (
    .pin13(Instructions_data[15]), .pin12(n7404_2_pin12));  // open: pin1, pin2, pin3, pin4, pin5, pin6, pin11, pin10, pin9, pin8
  _74138 #(.ShowInternalStructure("true")) u_74138_1 (
    .pin1(Instructions_data[12]), .pin2(Instructions_data[13]), .pin3(Instructions_data[14]),
    .pin4(n74138_1_pin4), .pin5(n74138_1_pin4), .pin6(n7404_2_pin12), .pin7(n74138_1_pin7),
    .pin15(n74138_1_pin15), .pin14(n74138_1_pin14), .pin13(n74138_1_pin13), .pin12(n74138_1_pin12),
    .pin11(n74138_1_pin11), .pin10(n74138_1_pin10), .pin9(n74138_1_pin9));
  _74138 #(.ShowInternalStructure("true")) u_74138_2 (
    .pin1(Instructions_data[12]), .pin2(Instructions_data[13]), .pin3(Instructions_data[14]),
    .pin4(n74138_2_pin4), .pin5(n74138_2_pin4), .pin6(Instructions_data[15]), .pin7(n74138_2_pin7),
    .pin15(n74138_2_pin15), .pin14(n74138_2_pin14), .pin13(n74138_2_pin13), .pin12(n74138_2_pin12),
    .pin11(n74138_2_pin11), .pin10(n74138_2_pin10), .pin9(n74138_2_pin9));
  _7404 #(.ShowInternalStructure("true")) u_7404_3 (
    .pin1(n74138_1_pin15), .pin2(n7404_3_pin2), .pin3(n74138_1_pin14), .pin4(n7404_3_pin4));  // open: pin5, pin6, pin13, pin12, pin11, pin10, pin9, pin8
  _7404 #(.ShowInternalStructure("true")) u_7404_4 (
    .pin1(n74138_1_pin10), .pin2(n7404_4_pin2), .pin3(n74138_1_pin9), .pin4(n7404_4_pin4),
    .pin5(n74138_1_pin7), .pin6(n7404_4_pin6), .pin13(n74138_1_pin13), .pin12(n7404_4_pin12),
    .pin11(n74138_1_pin12), .pin10(n7404_4_pin10), .pin9(n74138_1_pin11), .pin8(n7404_4_pin8));
  _7404 #(.ShowInternalStructure("true")) u_7404_5 (
    .pin1(n74138_2_pin12), .pin2(n7404_5_pin2), .pin3(n74138_2_pin11), .pin4(n7404_5_pin4),
    .pin5(n74138_2_pin10), .pin6(n7404_5_pin6), .pin13(n74138_2_pin15), .pin12(n7404_5_pin12),
    .pin11(n74138_2_pin14), .pin10(n7404_5_pin10), .pin9(n74138_2_pin13), .pin8(n7404_5_pin8));
  _7404 #(.ShowInternalStructure("true")) u_7404_6 (
    .pin13(n74138_2_pin9), .pin12(n7404_6_pin12), .pin11(n74138_2_pin7), .pin10(n7404_1_pin1));  // open: pin1, pin2, pin3, pin4, pin5, pin6, pin9, pin8
  _7432 #(.ShowInternalStructure("true")) u_7432_1 (
    .pin1(n7404_3_pin4), .pin2(n7404_4_pin12), .pin3(n7432_1_pin3), .pin4(n7404_4_pin12),
    .pin5(n7404_4_pin10), .pin6(n7432_1_pin6));  // open: pin13, pin12, pin11, pin10, pin9, pin8
  _7408 #(.ShowInternalStructure("true")) u_7408_2 (
    .pin13(n7404_4_pin8), .pin12(n7408_2_pin12), .pin11(n74157_1_pin1));  // open: pin1, pin2, pin3, pin4, pin5, pin6, pin10, pin9, pin8
  _7408 #(.ShowInternalStructure("true")) u_7408_3 (
    .pin13(n7408_1_pin8), .pin12(n7432_1_pin3), .pin11(n7408_3_pin11), .pin10(n7408_3_pin11),
    .pin9(n7408_3_pin9), .pin8(n7408_3_pin8));  // open: pin1, pin2, pin3, pin4, pin5, pin6
  _7404 #(.ShowInternalStructure("true")) u_7404_7 (
    .pin13(n7404_4_pin10), .pin12(n7404_7_pin12));  // open: pin1, pin2, pin3, pin4, pin5, pin6, pin11, pin10, pin9, pin8
  RAM #(.asyncread("true"), .clearpin("true"), .databus("bidir")) Stored_Variables (
    .addr(Instructions_data[7:0]), .we(n7404_4_pin10), .oe(n7404_7_pin12), .clk(n7408_1_pin8));  // open: data, clr
  TTY tty_1 (.data(n7474_12_pin9), .clk(n7408_1_pin8), .we(n7404_4_pin2));  // open: clr
  // Probe on {n7474_9_pin5[7], n7474_12_pin9}
  // Probe on {n7474_9_pin5[7], n7474_12_pin9}
  _74157 #(.ShowInternalStructure("true")) u_74157_5 (
    .pin1(n7432_1_pin6), .pin2(Instructions_data[0]), .pin3(n74157_5_pin3), .pin4(n74157_5_pin4[0]),
    .pin5(Instructions_data[1]), .pin6(n74157_5_pin6), .pin7(n74157_5_pin4[1]), .pin14(Instructions_data[3]),
    .pin13(n74157_5_pin13), .pin12(n74157_5_pin4[3]), .pin11(Instructions_data[2]), .pin10(n74157_5_pin10),
    .pin9(n74157_5_pin4[2]));  // open: pin15
  _74245 #(.ShowInternalStructure("true")) u_74245_1 (
    .pin1(n74245_1_pin1), .pin2(n74245_1_pin2[0]), .pin3(n74245_1_pin2[1]), .pin4(n74245_1_pin2[2]),
    .pin5(n74245_1_pin2[3]), .pin6(n74245_1_pin2[4]), .pin7(n74245_1_pin2[5]), .pin8(n74245_1_pin2[6]),
    .pin9(n74245_1_pin2[7]), .pin19(n7404_4_pin10), .pin18(n74157_5_pin3), .pin17(n74157_5_pin6),
    .pin16(n74157_5_pin10), .pin15(n74157_5_pin13), .pin14(n74245_1_pin14), .pin13(n74245_1_pin13),
    .pin12(n74245_1_pin12), .pin11(n74245_1_pin11));
  _7474 #(.ShowInternalStructure("true")) u_7474_9 (
    .pin2(n7474_12_pin12[7]), .pin3(n7408_3_pin8), .pin5(n7474_9_pin5[7]), .pin12(n7474_12_pin12[6]),
    .pin11(n7408_3_pin8), .pin9(n7474_12_pin9[6]));  // open: pin1, pin4, pin6, pin13, pin10, pin8
  _7474 #(.ShowInternalStructure("true")) u_7474_10 (
    .pin2(n7474_12_pin12[3]), .pin3(n7408_3_pin8), .pin5(n7474_12_pin9[3]), .pin12(n7474_12_pin12[2]),
    .pin11(n7408_3_pin8), .pin9(n7474_12_pin9[2]));  // open: pin1, pin4, pin6, pin13, pin10, pin8
  _7432 #(.ShowInternalStructure("true")) u_7432_2 (
    .pin10(n7432_2_pin10), .pin9(n7432_2_pin9), .pin8(n7408_2_pin12));  // open: pin1, pin2, pin3, pin4, pin5, pin6, pin13, pin12, pin11
  _74157 #(.ShowInternalStructure("true")) u_74157_6 (
    .pin1(n7432_1_pin6), .pin2(Instructions_data[4]), .pin3(n74245_1_pin14), .pin4(n74157_5_pin4[4]),
    .pin5(Instructions_data[5]), .pin6(n74245_1_pin13), .pin7(n74157_5_pin4[5]),
    .pin14(Instructions_data[7]), .pin13(n74245_1_pin11), .pin12(n74157_5_pin4[7]),
    .pin11(Instructions_data[6]), .pin10(n74245_1_pin12), .pin9(n74157_5_pin4[6]));  // open: pin15
  _7486 #(.ShowInternalStructure("true")) u_7486_1 (
    .pin10(n7486_1_pin10), .pin9(n7486_1_pin9), .pin8(n7432_2_pin10));  // open: pin1, pin2, pin3, pin4, pin5, pin6, pin13, pin12, pin11
  _7486 #(.ShowInternalStructure("true")) u_7486_2 (
    .pin10(n7486_2_pin10), .pin9(n7486_2_pin9), .pin8(n7432_2_pin9));  // open: pin1, pin2, pin3, pin4, pin5, pin6, pin13, pin12, pin11
  _7474 #(.ShowInternalStructure("true")) u_7474_11 (
    .pin2(n7474_12_pin12[5]), .pin3(n7408_3_pin8), .pin5(n7474_12_pin9[5]), .pin12(n7474_12_pin12[4]),
    .pin11(n7408_3_pin8), .pin9(n7474_12_pin9[4]));  // open: pin1, pin4, pin6, pin13, pin10, pin8
  _7474 #(.ShowInternalStructure("true")) u_7474_12 (
    .pin2(n7474_12_pin12[1]), .pin3(n7408_3_pin8), .pin5(n7474_12_pin9[1]), .pin12(n7474_12_pin12[0]),
    .pin11(n7408_3_pin8), .pin9(n7474_12_pin9[0]));  // open: pin1, pin4, pin6, pin13, pin10, pin8
  _74245 #(.ShowInternalStructure("true")) u_74245_2 (
    .pin1(n74245_2_pin1), .pin2(n74245_1_pin2[0]), .pin3(n74245_1_pin2[1]), .pin4(n74245_1_pin2[2]),
    .pin5(n74245_1_pin2[3]), .pin6(n74245_1_pin2[4]), .pin7(n74245_1_pin2[5]), .pin8(n74245_1_pin2[6]),
    .pin9(n74245_1_pin2[7]), .pin19(n7404_7_pin12), .pin18(n7474_12_pin9[0]), .pin17(n7474_12_pin9[1]),
    .pin16(n7474_12_pin9[2]), .pin15(n7474_12_pin9[3]), .pin14(n7474_12_pin9[4]), .pin13(n7474_12_pin9[5]),
    .pin12(n7474_12_pin9[6]), .pin11(n7474_9_pin5[7]));
  _7408 #(.ShowInternalStructure("true")) u_7408_4 (
    .pin10(n7486_1_pin10), .pin9(n7408_4_pin9), .pin8(n7486_1_pin9));  // open: pin1, pin2, pin3, pin4, pin5, pin6, pin13, pin12, pin11
  _7408 #(.ShowInternalStructure("true")) u_7408_5 (
    .pin10(n7486_2_pin10), .pin9(n7408_5_pin9), .pin8(n7486_2_pin9));  // open: pin1, pin2, pin3, pin4, pin5, pin6, pin13, pin12, pin11
  _7485 #(.ShowInternalStructure("true")) u_7485_1 (
    .pin1(n7485_1_pin1), .pin5(n7486_1_pin10), .pin7(n7408_4_pin9), .pin15(n7474_12_pin9[0]),
    .pin14(n7485_1_pin1), .pin13(n7474_12_pin9[1]), .pin12(n7474_12_pin9[2]), .pin11(n7485_1_pin1),
    .pin10(n7474_12_pin9[3]), .pin9(n7485_1_pin1));  // open: pin2, pin3, pin4, pin6
  _7485 #(.ShowInternalStructure("true")) u_7485_2 (
    .pin1(n7485_2_pin1), .pin5(n7486_2_pin10), .pin7(n7408_5_pin9), .pin15(n7474_12_pin9[4]),
    .pin14(n7485_2_pin1), .pin13(n7474_12_pin9[5]), .pin12(n7474_12_pin9[6]), .pin11(n7485_2_pin1),
    .pin10(n7474_9_pin5[7]), .pin9(n7485_2_pin1));  // open: pin2, pin3, pin4, pin6
  // Probe on n74157_5_pin4
  // Probe on n74157_5_pin4
  // Probe on n7474_12_pin12
  // Probe on n7474_12_pin12
  // Probe on {n7474_9_pin5[7], n7474_12_pin9}
  // Probe on {n7474_9_pin5[7], n7474_12_pin9}
  _74283 #(.ShowInternalStructure("true")) u_74283_1 (
    .pin1(n74283_1_pin4[1]), .pin2(n74157_5_pin4[1]), .pin3(n7474_12_pin9[1]), .pin4(n74283_1_pin4[0]),
    .pin5(n7474_12_pin9[0]), .pin6(n74157_5_pin4[0]), .pin15(n74157_5_pin4[2]), .pin14(n7474_12_pin9[2]),
    .pin13(n74283_1_pin4[2]), .pin12(n7474_12_pin9[3]), .pin11(n74157_5_pin4[3]), .pin10(n74283_1_pin4[3]),
    .pin9(n74283_1_pin9));  // open: pin7
  _74283 #(.ShowInternalStructure("true")) u_74283_2 (
    .pin1(n74283_1_pin4[5]), .pin2(n74157_5_pin4[5]), .pin3(n7474_12_pin9[5]), .pin4(n74283_1_pin4[4]),
    .pin5(n7474_12_pin9[4]), .pin6(n74157_5_pin4[4]), .pin7(n74283_1_pin9), .pin15(n74157_5_pin4[6]),
    .pin14(n7474_12_pin9[6]), .pin13(n74283_1_pin4[6]), .pin12(n7474_9_pin5[7]), .pin11(n74157_5_pin4[7]),
    .pin10(n74283_1_pin4[7]), .pin9(n74283_2_pin9[8]));
  _7485 #(.ShowInternalStructure("true")) u_7485_3 (
    .pin1(n74157_5_pin4[3]), .pin5(n7485_3_pin5), .pin7(n7485_3_pin7), .pin15(n7474_12_pin9[3]),
    .pin14(n74157_5_pin4[2]), .pin13(n7474_12_pin9[2]), .pin12(n7474_12_pin9[1]), .pin11(n74157_5_pin4[1]),
    .pin10(n7474_12_pin9[0]), .pin9(n74157_5_pin4[0]));  // open: pin2, pin3, pin4, pin6
  _7485 #(.ShowInternalStructure("true")) u_7485_4 (
    .pin1(n74157_5_pin4[7]), .pin5(n7485_4_pin5), .pin7(n7485_4_pin7), .pin15(n7474_9_pin5[7]),
    .pin14(n74157_5_pin4[6]), .pin13(n7474_12_pin9[6]), .pin12(n7474_12_pin9[5]), .pin11(n74157_5_pin4[5]),
    .pin10(n7474_12_pin9[4]), .pin9(n74157_5_pin4[4]));  // open: pin2, pin3, pin4, pin6
  _7408 #(.ShowInternalStructure("true")) u_7408_6 (
    .pin1(n7474_12_pin9[0]), .pin2(n74157_5_pin4[0]), .pin3(n7408_6_pin3[0]), .pin4(n7474_12_pin9[1]),
    .pin5(n74157_5_pin4[1]), .pin6(n7408_6_pin3[1]), .pin13(n7474_12_pin9[2]), .pin12(n74157_5_pin4[2]),
    .pin11(n7408_6_pin3[2]), .pin10(n7474_12_pin9[3]), .pin9(n74157_5_pin4[3]), .pin8(n7408_6_pin3[3]));
  _7408 #(.ShowInternalStructure("true")) u_7408_7 (
    .pin1(n7474_12_pin9[4]), .pin2(n74157_5_pin4[4]), .pin3(n7408_6_pin3[4]), .pin4(n7474_12_pin9[5]),
    .pin5(n74157_5_pin4[5]), .pin6(n7408_6_pin3[5]), .pin13(n7474_12_pin9[6]), .pin12(n74157_5_pin4[6]),
    .pin11(n7408_6_pin3[6]), .pin10(n7474_9_pin5[7]), .pin9(n74157_5_pin4[7]), .pin8(n7408_6_pin3[7]));
  LED led_1 (.in(n74283_2_pin9[8]));
  _7408 #(.ShowInternalStructure("true")) u_7408_8 (
    .pin4(n7485_3_pin7), .pin5(n7485_3_pin5), .pin6(n7408_8_pin6));  // open: pin1, pin2, pin3, pin13, pin12, pin11, pin10, pin9, pin8
  _7408 #(.ShowInternalStructure("true")) u_7408_9 (
    .pin1(n7485_3_pin5), .pin2(n7485_4_pin7), .pin3(n7408_9_pin3), .pin4(n7485_4_pin7), .pin5(n7485_4_pin5),
    .pin6(n7408_9_pin6), .pin13(n7408_9_pin3), .pin12(n7408_9_pin12), .pin11(n7408_9_pin11));  // open: pin10, pin9, pin8
  _7486 #(.ShowInternalStructure("true")) u_7486_3 (
    .pin1(n7474_12_pin9[0]), .pin2(n74157_5_pin4[0]), .pin3(n7486_3_pin3[0]), .pin4(n7474_12_pin9[1]),
    .pin5(n74157_5_pin4[1]), .pin6(n7486_3_pin3[1]), .pin13(n7474_12_pin9[2]), .pin12(n74157_5_pin4[2]),
    .pin11(n7486_3_pin3[2]), .pin10(n7474_12_pin9[3]), .pin9(n74157_5_pin4[3]), .pin8(n7486_3_pin3[3]));
  _7486 #(.ShowInternalStructure("true")) u_7486_4 (
    .pin1(n7474_12_pin9[4]), .pin2(n74157_5_pin4[4]), .pin3(n7486_3_pin3[4]), .pin4(n7474_12_pin9[5]),
    .pin5(n74157_5_pin4[5]), .pin6(n7486_3_pin3[5]), .pin13(n7474_12_pin9[6]), .pin12(n74157_5_pin4[6]),
    .pin11(n7486_3_pin3[6]), .pin10(n7474_9_pin5[7]), .pin9(n74157_5_pin4[7]), .pin8(n7486_3_pin3[7]));
  _7486 #(.ShowInternalStructure("true")) u_7486_5 (
    .pin4(n7485_3_pin5), .pin5(n7408_8_pin6), .pin6(n7408_9_pin12));  // open: pin1, pin2, pin3, pin13, pin12, pin11, pin10, pin9, pin8
  _7486 #(.ShowInternalStructure("true")) u_7486_6 (
    .pin4(n7485_4_pin5), .pin5(n7408_9_pin6), .pin6(n7486_6_pin6));  // open: pin1, pin2, pin3, pin13, pin12, pin11, pin10, pin9, pin8
  // Probe on n74157_5_pin4
  // Probe on {n7474_9_pin5[7], n7474_12_pin9}
  // Probe on {n74283_2_pin9[8], n74283_1_pin4}
  _7432 #(.ShowInternalStructure("true")) u_7432_3 (
    .pin1(n7408_9_pin11), .pin2(n7486_6_pin6), .pin3(n7432_3_pin3));  // open: pin4, pin5, pin6, pin13, pin12, pin11, pin10, pin9, pin8
  // Probe on n74157_5_pin4
  // Probe on {n7474_9_pin5[7], n7474_12_pin9}
  // Probe on {n74283_2_pin9[8], n74283_1_pin4}
  // Probe on n7486_3_pin3
  // Probe on n7486_3_pin3
  // Probe on n7408_6_pin3
  // Probe on n7408_6_pin3
  _74151 #(.ShowInternalStructure("true")) u_74151_1 (
    .pin1(n7486_3_pin3[7]), .pin2(n7408_6_pin3[7]), .pin3(n74283_1_pin4[7]), .pin4(n74157_5_pin4[7]),
    .pin5(n7474_12_pin12[7]), .pin11(Instructions_data[8]), .pin10(Instructions_data[9]),
    .pin9(Instructions_data[10]));  // open: pin6, pin7, pin15, pin14, pin13, pin12
  _74151 #(.ShowInternalStructure("true")) u_74151_2 (
    .pin1(n7486_3_pin3[6]), .pin2(n7408_6_pin3[6]), .pin3(n74283_1_pin4[6]), .pin4(n74157_5_pin4[6]),
    .pin5(n7474_12_pin12[6]), .pin11(Instructions_data[8]), .pin10(Instructions_data[9]),
    .pin9(Instructions_data[10]));  // open: pin6, pin7, pin15, pin14, pin13, pin12
  _74151 #(.ShowInternalStructure("true")) u_74151_3 (
    .pin1(n7486_3_pin3[5]), .pin2(n7408_6_pin3[5]), .pin3(n74283_1_pin4[5]), .pin4(n74157_5_pin4[5]),
    .pin5(n7474_12_pin12[5]), .pin11(Instructions_data[8]), .pin10(Instructions_data[9]),
    .pin9(Instructions_data[10]));  // open: pin6, pin7, pin15, pin14, pin13, pin12
  _74151 #(.ShowInternalStructure("true")) u_74151_4 (
    .pin1(n7486_3_pin3[4]), .pin2(n7408_6_pin3[4]), .pin3(n74283_1_pin4[4]), .pin4(n74157_5_pin4[4]),
    .pin5(n7474_12_pin12[4]), .pin11(Instructions_data[8]), .pin10(Instructions_data[9]),
    .pin9(Instructions_data[10]));  // open: pin6, pin7, pin15, pin14, pin13, pin12
  _74151 #(.ShowInternalStructure("true")) u_74151_5 (
    .pin1(n7486_3_pin3[3]), .pin2(n7408_6_pin3[3]), .pin3(n74283_1_pin4[3]), .pin4(n74157_5_pin4[3]),
    .pin5(n7474_12_pin12[3]), .pin11(Instructions_data[8]), .pin10(Instructions_data[9]),
    .pin9(Instructions_data[10]));  // open: pin6, pin7, pin15, pin14, pin13, pin12
  _74151 #(.ShowInternalStructure("true")) u_74151_6 (
    .pin1(n7486_3_pin3[2]), .pin2(n7408_6_pin3[2]), .pin3(n74283_1_pin4[2]), .pin4(n74157_5_pin4[2]),
    .pin5(n7474_12_pin12[2]), .pin11(Instructions_data[8]), .pin10(Instructions_data[9]),
    .pin9(Instructions_data[10]));  // open: pin6, pin7, pin15, pin14, pin13, pin12
  _74151 #(.ShowInternalStructure("true")) u_74151_7 (
    .pin1(n7486_3_pin3[1]), .pin2(n7408_6_pin3[1]), .pin3(n74283_1_pin4[1]), .pin4(n74157_5_pin4[1]),
    .pin5(n7474_12_pin12[1]), .pin11(Instructions_data[8]), .pin10(Instructions_data[9]),
    .pin9(Instructions_data[10]));  // open: pin6, pin7, pin15, pin14, pin13, pin12
  _74151 #(.ShowInternalStructure("true")) u_74151_8 (
    .pin1(n7486_3_pin3[0]), .pin2(n7408_6_pin3[0]), .pin3(n74283_1_pin4[0]), .pin4(n74157_5_pin4[0]),
    .pin5(n7474_12_pin12[0]), .pin14(n7432_3_pin3), .pin11(Instructions_data[8]),
    .pin10(Instructions_data[9]), .pin9(Instructions_data[10]));  // open: pin6, pin7, pin15, pin13, pin12
  // also tied to GND on the sheet: {n74157_3_pin3, n74138_2_pin4, n74138_1_pin4, n74245_2_pin1, n7485_1_pin1, n7485_2_pin1}
  // also tied to VCC on the sheet: {n7408_3_pin9, n74245_1_pin1}

  // Notes on the sheet:
  //   Stop
  //   Program Counter
  //   contents of Instructions (hex, n*v repeats v):
  //   2000 5000 2001 5000 2002 5000 5000 2003 5000 2004 5000 2005 5000 2003 5000 2006 5000 2007 5000 f000
  //   As in just connecting the pins to the same place without a Multiplexer
  //   Instructions Decoder
  //   I think this'll be fine when connecting it on the bread board pins but who knows, I'll see if it blows up
  //   ALU Operations
  //   0 - Connect to ground
  //   Stop
  //   I think I messed up, I think I need to use the 1a for the d flip flop gate signal and 1b for the branch instruction but figure this out in the morning
  //   Output Character
  //   Write to Accumalator
  //   Use Memory
  //   Write Memory
  //   Experiment but idk what I was doing with the AND and XOR gates but I am also doing this at 5 in the morning so idk if either are right but I think using the 74hc157 is a simpler way then what ever the fuck I was doing
  //   Branch if Not Equal to Zero
  //   0
  //   7
  //   Problem - ACC gets written to even when not wanted
  //   Solution (kinda) - add a bit and the output to the and
  //   idk why this works but I think the issue is a delay
  //   Output
  //   7
  //   Accumalator
  //   From ACC
  //   Input 2
  //   ALU Operation
  //   0
  //   From ACC
  //   Input
  //   7
  //   From ACC
  //   Input 2
  //   3
  //   0
  //   I dont have a bit shifter but I would like to put that here
  //   ALU to ACC
  //   7
  //   0
  //   XOR
  //   AND
  //   Idk but I don't need more than 8 ALU operatios so I don't need the spare bit but if I did then it's always here to expand upon
  //   7
  //   0
  //   ALU to ACC
endmodule
