// Logisim project SimpleCPU.circ as structural Verilog: 4 circuits, main circuit CPU_main
module CPU_main (
);

  wire and_1_out, and_2_out, clock_1_out, comparator_1_lt, comparator_2_gt, instruction_decoding_unit_1_bnez,
       instruction_decoding_unit_1_output_char, instruction_decoding_unit_1_stop,
       instruction_decoding_unit_1_use_memory, instruction_decoding_unit_1_write_acc,
       instruction_decoding_unit_1_write_memory, not_1_out;
  wire [3:0] instruction_decoding_unit_1_alu_operation;
  wire [6:0] ACC_q;
  wire [7:0] acc_hex_to_ascii_1_hex_output_big, acc_hex_to_ascii_1_hex_output_small, adder_1_out,
       adder_2_out, and_3_out, bit_extender_1_out, instruction_decoding_unit_1_addr_or_imm,
       multiplexer_1_out, multiplexer_2_out, multiplexer_3_out, PC_q, shifter_1_out, Stored_Variables_dout,
       xor_1_out;
  wire [7:7] ACC_q_2;
  wire [15:0] Instructions_data;

  Adder adder_1 (.a(PC_q), .b(8'h1), .out(adder_1_out));  // open: cin, cout
  Clock clock_1 (.out(clock_1_out));
  Register PC (.D(multiplexer_1_out), .clk(and_1_out), .Q(PC_q));  // open: en, clr
  Multiplexer #(.width(8)) multiplexer_1 (
    .in0(adder_1_out), .in1(instruction_decoding_unit_1_addr_or_imm), .out(multiplexer_1_out), .sel(and_2_out));
  Instruction_Decoding_Unit instruction_decoding_unit_1 (
    .Instruction(Instructions_data), .ALU_Operation(instruction_decoding_unit_1_alu_operation),
    .Write_ACC(instruction_decoding_unit_1_write_acc), .Use_Memory(instruction_decoding_unit_1_use_memory),
    .Write_Memory(instruction_decoding_unit_1_write_memory), .BNEZ(instruction_decoding_unit_1_bnez),
    .Output_Char(instruction_decoding_unit_1_output_char), .Stop(instruction_decoding_unit_1_stop),
    .Addr_or_Imm(instruction_decoding_unit_1_addr_or_imm));
  not not_1 (not_1_out, instruction_decoding_unit_1_stop);
  and and_1 (and_1_out, clock_1_out, not_1_out);
  TTY tty_1 (.data(ACC_q), .clk(clock_1_out), .we(instruction_decoding_unit_1_output_char));  // open: clr
  ROM #(.dataWidth(16)) Instructions (.addr(PC_q), .data(Instructions_data));
  and and_2 (and_2_out, instruction_decoding_unit_1_bnez, comparator_2_gt);
  RAM #(.asyncread("true"), .clearpin("true")) Stored_Variables (
    .addr(instruction_decoding_unit_1_addr_or_imm), .we(instruction_decoding_unit_1_write_memory),
    .clk(and_1_out), .din({ACC_q_2[7], ACC_q}), .dout(Stored_Variables_dout));  // open: oe, clr
  Register ACC (
    .D(multiplexer_3_out), .en(instruction_decoding_unit_1_write_acc), .clk(and_1_out),
    .Q({ACC_q_2[7], ACC_q}));  // open: clr
  // Probe on instruction_decoding_unit_1_addr_or_imm
  // Probe on instruction_decoding_unit_1_addr_or_imm
  // Probe on {ACC_q_2[7], ACC_q}
  // Probe on {ACC_q_2[7], ACC_q}
  Multiplexer #(.width(8)) multiplexer_2 (
    .in0(instruction_decoding_unit_1_addr_or_imm), .in1(Stored_Variables_dout), .out(multiplexer_2_out),
    .sel(instruction_decoding_unit_1_use_memory));
  // Probe on multiplexer_2_out
  // Probe on multiplexer_2_out
  // Probe on Stored_Variables_dout
  // Probe on Stored_Variables_dout
  // Probe on {ACC_q_2[7], ACC_q}
  // Probe on {ACC_q_2[7], ACC_q}
  // Probe on multiplexer_2_out
  // Probe on multiplexer_2_out
  // Probe on multiplexer_3_out
  // Probe on multiplexer_3_out
  // Probe on {ACC_q_2[7], ACC_q}
  // Probe on {ACC_q_2[7], ACC_q}
  Comparator #(.mode("unsigned")) comparator_1 (
    .a({ACC_q_2[7], ACC_q}), .b(multiplexer_2_out), .lt(comparator_1_lt));  // open: gt, eq
  Adder adder_2 (.a({ACC_q_2[7], ACC_q}), .b(multiplexer_2_out), .out(adder_2_out));  // open: cin, cout
  assign and_3_out = {ACC_q_2[7], ACC_q} & multiplexer_2_out;  // AND_Gate and_3, 8 bits wide
  assign xor_1_out = {ACC_q_2[7], ACC_q} ^ multiplexer_2_out;  // XOR_Gate xor_1, 8 bits wide
  Shifter #(.shift("lr")) shifter_1 (.in(multiplexer_2_out), .\dist (3'b100), .out(shifter_1_out));
  assign bit_extender_1_out = {{7{1'b0}}, comparator_1_lt};  // Bit_Extender bit_extender_1
  Comparator #(.mode("unsigned")) comparator_2 (
    .a({ACC_q_2[7], ACC_q}), .b({8{1'b0}}), .gt(comparator_2_gt));  // open: eq, lt
  // Probe on adder_2_out
  // Probe on adder_2_out
  // Probe on and_3_out
  // Probe on and_3_out
  // Probe on xor_1_out
  // Probe on xor_1_out
  ACC_Hex_to_ASCII acc_hex_to_ascii_1 (
    .ACC({ACC_q_2[7], ACC_q}), .Hex_Output_Small(acc_hex_to_ascii_1_hex_output_small),
    .Hex_Output_Big(acc_hex_to_ascii_1_hex_output_big));
  Multiplexer #(.select(4), .width(8)) multiplexer_3 (
    .in0(multiplexer_2_out), .in1(adder_2_out), .in2(and_3_out), .in3(xor_1_out), .in4(shifter_1_out),
    .in5(bit_extender_1_out), .in6(acc_hex_to_ascii_1_hex_output_small),
    .in7(acc_hex_to_ascii_1_hex_output_big), .out(multiplexer_3_out),
    .sel(instruction_decoding_unit_1_alu_operation));  // open: in8, in9, in10, in11, in12, in13, in14, in15

  // Notes on the sheet:
  //   contents of Instructions (hex, n*v repeats v):
  //   2000 5000 2001 5000 2002 5000 5000 2003 5000 2004 5000 2005 5000 2003 5000 2006 5000 2007 5000 f000
  //   Student id: 24814364
endmodule

module Instruction_Decoding_Unit (
  input  [15:0] Instruction,
  output [3:0] ALU_Operation,
  output Write_ACC,
  output Use_Memory,
  output Write_Memory,
  output BNEZ,
  output Output_Char,
  output Stop,
  output [7:0] Addr_or_Imm
);

  wire decoder_1_out1, decoder_1_out2;

  Decoder #(.select(4)) decoder_1 (
    .out1(decoder_1_out1), .out2(decoder_1_out2), .out3(Write_Memory), .out4(BNEZ), .out5(Output_Char),
    .out15(Stop), .sel(Instruction[15:12]));  // open: out0, out6, out7, out8, out9, out10, out11, out12, out13, out14, en
  or or_1 (Write_ACC, decoder_1_out1, decoder_1_out2);
  or or_2 (Use_Memory, decoder_1_out2, Write_Memory);

  assign Addr_or_Imm = Instruction[7:0];
  assign ALU_Operation = Instruction[11:8];
endmodule

module ALU (
  input  [3:0] ALU_Operation,
  input  [7:0] From_ACC,
  input  [7:0] Input2,
  output [7:0] ALU_to_ACC,
  output ACC_NE_Zero
);

  wire comparator_1_lt;
  wire [7:0] acc_hex_to_ascii_1_hex_output_big, acc_hex_to_ascii_1_hex_output_small, adder_1_out, and_1_out,
       bit_extender_1_out, shifter_1_out, xor_1_out;

  Comparator #(.mode("unsigned")) comparator_1 (.a(From_ACC), .b(Input2), .lt(comparator_1_lt));  // open: gt, eq
  Comparator #(.mode("unsigned")) comparator_2 (.a(From_ACC), .b({8{1'b0}}), .gt(ACC_NE_Zero));  // open: eq, lt
  Adder adder_1 (.a(From_ACC), .b(Input2), .out(adder_1_out));  // open: cin, cout
  assign and_1_out = From_ACC & Input2;  // AND_Gate and_1, 8 bits wide
  assign xor_1_out = From_ACC ^ Input2;  // XOR_Gate xor_1, 8 bits wide
  Shifter #(.shift("lr")) shifter_1 (.in(Input2), .\dist (3'b100), .out(shifter_1_out));
  assign bit_extender_1_out = {{7{1'b0}}, comparator_1_lt};  // Bit_Extender bit_extender_1
  ACC_Hex_to_ASCII acc_hex_to_ascii_1 (
    .ACC(From_ACC), .Hex_Output_Small(acc_hex_to_ascii_1_hex_output_small),
    .Hex_Output_Big(acc_hex_to_ascii_1_hex_output_big));
  Multiplexer #(.select(4), .width(8)) multiplexer_1 (
    .in0(Input2), .in1(adder_1_out), .in2(and_1_out), .in3(xor_1_out), .in4(shifter_1_out),
    .in5(bit_extender_1_out), .in6(acc_hex_to_ascii_1_hex_output_small),
    .in7(acc_hex_to_ascii_1_hex_output_big), .out(ALU_to_ACC), .sel(ALU_Operation));  // open: in8, in9, in10, in11, in12, in13, in14, in15
endmodule

module ACC_Hex_to_ASCII (
  input  [7:0] ACC,
  output [7:0] Hex_Output_Small,
  output [7:0] Hex_Output_Big
);

  wire comparator_1_lt, comparator_2_lt, not_1_out, not_2_out;
  wire [3:0] adder_1_out, adder_2_out;

  not not_1 (not_1_out, comparator_1_lt);
  Comparator comparator_1 (.a({4'b0011, ACC[7:4]}), .b(8'h3a), .lt(comparator_1_lt));  // open: gt, eq
  Adder #(.width(4)) adder_1 (.a(ACC[7:4]), .b(4'b0111), .out(adder_1_out));  // open: cin, cout
  Comparator comparator_2 (.a({4'b0011, ACC[3:0]}), .b(8'h3a), .lt(comparator_2_lt));  // open: gt, eq
  not not_2 (not_2_out, comparator_2_lt);
  Adder #(.width(4)) adder_2 (.a(ACC[3:0]), .b(4'b0111), .out(adder_2_out));  // open: cin, cout
  Multiplexer #(.width(8)) multiplexer_1 (
    .in0({4'b0011, ACC[7:4]}), .in1({4'b0110, adder_1_out}), .out(Hex_Output_Big), .sel(not_1_out));
  Multiplexer #(.width(8)) multiplexer_2 (
    .in0({4'b0011, ACC[3:0]}), .in1({4'b0110, adder_2_out}), .out(Hex_Output_Small), .sel(not_2_out));
endmodule
